// Logisim project ALU (Add , Sub and Multiplication).circ as structural Verilog: 1 circuit, main circuit main
module main (
  input  [1:0] in_1,
  input  in_2,
  input  in_3,
  input  in_4,
  input  in_5,
  input  in_6,
  input  in_7,
  input  in_8,
  input  in_9,
  input  in_10,
  input  in_11,
  input  in_12,
  input  in_13,
  input  in_14,
  input  in_15,
  input  in_16,
  input  in_17,
  input  in_18,
  input  in_19,
  input  in_20,
  input  in_21,
  input  in_22,
  input  in_23,
  input  in_24,
  input  in_25,
  input  in_26,
  input  in_27,
  input  in_28,
  input  in_29,
  input  in_30,
  input  in_31,
  input  in_32,
  input  in_33,
  input  in_34,
  input  in_35,
  input  in_36,
  input  in_37,
  input  in_38,
  input  in_39,
  input  in_40,
  input  in_41,
  input  in_42,
  input  in_43,
  input  in_44,
  input  in_45,
  input  in_46,
  input  in_47,
  input  in_48,
  input  in_49,
  input  in_50,
  input  in_51,
  input  in_52,
  input  in_53,
  input  in_54,
  input  in_55,
  input  in_56,
  input  in_57,
  input  in_58,
  input  in_59,
  input  in_60,
  input  in_61,
  input  in_62,
  input  in_63,
  input  in_64,
  input  in_65,
  input  in_66,
  input  in_67,
  input  in_68,
  input  in_69,
  input  in_70,
  input  in_71,
  input  in_72,
  input  in_73,
  input  in_74,
  input  in_75,
  input  in_76,
  input  in_77,
  input  in_78,
  input  in_79,
  input  in_80,
  input  in_81,
  input  in_82,
  input  in_83,
  input  in_84,
  input  in_85,
  input  in_86,
  input  in_87,
  input  in_88,
  input  in_89,
  input  in_90,
  input  in_91,
  input  in_92,
  input  in_93,
  input  in_94,
  input  in_95,
  input  in_96,
  input  in_97,
  input  in_98,
  input  in_99,
  input  in_100,
  input  in_101,
  input  in_102,
  input  in_103,
  input  in_104,
  input  in_105,
  input  in_106,
  input  in_107,
  input  in_108,
  input  in_109,
  input  in_110,
  input  in_111,
  input  in_112,
  input  in_113,
  input  in_114,
  input  in_115,
  input  in_116,
  input  in_117,
  input  in_118,
  input  in_119,
  input  in_120,
  input  in_121,
  input  in_122,
  input  in_123,
  input  in_124,
  input  in_125,
  input  in_126,
  input  in_127,
  input  in_128,
  input  in_129,
  input  in_130,
  input  in_131,
  input  in_132,
  input  in_133,
  input  in_134,
  input  in_135,
  input  in_136,
  output out_137,
  output out_138,
  output out_139,
  output out_140,
  output out_141,
  output out_142,
  output out_143,
  output out_144,
  output out_145,
  output out_146,
  output out_147,
  output out_148,
  output out_149,
  output out_150,
  output out_151,
  output out_152,
  output out_153,
  output out_154,
  output out_155,
  output out_156,
  output out_157,
  output out_158,
  output out_159,
  output out_160,
  output out_161,
  output out_162,
  output out_163,
  output out_164,
  output out_165,
  output out_166,
  output out_167,
  output out_168,
  output out_169,
  output out_170,
  output out_171,
  output out_172,
  output out_173,
  output out_174,
  output out_175,
  output out_176,
  output out_177,
  output out_178,
  output out_179,
  output out_180,
  output out_181,
  output out_182,
  output out_183,
  output out_184,
  output out_185,
  output out_186,
  output out_187,
  output out_188,
  output out_189,
  output out_190,
  output out_191,
  output out_192,
  output out_193,
  output out_194,
  output out_195,
  output out_196,
  output out_197,
  output out_198,
  output out_199,
  output out_200,
  output out_201,
  output out_202,
  output out_203,
  output out_204,
  output out_205,
  output out_206,
  output out_207,
  output out_208,
  output out_209,
  output out_210,
  output out_211,
  output out_212,
  output out_213,
  output out_214,
  output out_215,
  output out_216,
  output out_217,
  output out_218,
  output out_219,
  output out_220,
  output out_221,
  output out_222,
  output out_223,
  output out_224,
  output out_225,
  output out_226,
  output out_227,
  output out_228,
  output out_229,
  output out_230,
  output out_231,
  output out_232,
  output out_233,
  output out_234,
  output out_235,
  output out_236,
  output out_237,
  output out_238,
  output out_239,
  output out_240,
  output out_241,
  output out_242,
  output out_243,
  output out_244,
  output out_245,
  output out_246,
  output out_247,
  output out_248,
  output out_249,
  output out_250,
  output out_251,
  output out_252,
  output out_253,
  output out_254,
  output out_255,
  output out_256,
  output out_257,
  output out_258,
  output out_259,
  output out_260,
  output out_261,
  output out_262,
  output out_263,
  output out_264,
  output out_265,
  output [15:0] out_266,
  output [15:0] out_267,
  output [15:0] out_268,
  output [15:0] out_269,
  output [15:0] out_270,
  output [15:0] out_271,
  output [15:0] out_272,
  output [15:0] out_273
);

  wire adder_1_cout, adder_2_cout, adder_3_cout, adder_4_cout, adder_5_cout, adder_6_cout, adder_8_cout,
       adder_9_cout, adder_10_cout, adder_11_cout, adder_12_cout, adder_14_cout, adder_15_cout,
       adder_16_cout, adder_18_cout, adder_19_cout, adder_20_cout, adder_21_cout, adder_22_cout,
       adder_24_cout, adder_25_cout, adder_26_cout, adder_29_cout, adder_30_cout, adder_32_cout,
       subtractor_1_bout, subtractor_2_bout, subtractor_3_bout;
  wire [0:0] A5, adder_13_cout, adder_27_cout, adder_28_cout, adder_31_cout, adder_33_cout, S5;
  wire [15:0] A1, A2, A3, A4, adder_1_out, adder_2_out, adder_3_out, adder_4_out, adder_5_out, adder_6_out,
       adder_7_out, adder_9_out, adder_10_out, adder_11_out, adder_12_out, adder_13_out, adder_18_out,
       adder_19_out, adder_20_out, adder_21_out, adder_22_out, adder_25_out, adder_26_out, adder_27_out,
       adder_29_out, adder_30_out, AE0, AE1, EB0, EB1, EC0, EC1, ED0, ED1, FA0, FA1, FB0, FB1, FC0, FC1, FD0,
       FD1, GA0, GA1, GB0, GB1, GC0, GC1, GD0, GD1, HA0, HA1, HB0, HB1, HC0, HC1, HD0, HD1, M2, M3, M4, M5,
       M6, M7, M8, S1, S2, S3, S4;

  Multiplexer #(.select(2), .width(16), .enable("false")) multiplexer_1 (
    .in2(M8),
    .out({out_137, out_138, out_139, out_140, out_141, out_142, out_143, out_144, out_145, out_146, out_147, out_148, out_149, out_150, out_151, out_152}),
    .sel(in_1));  // open: in0, in1, in3
  Multiplexer #(.select(2), .width(16), .enable("false")) multiplexer_2 (
    .in2(M7),
    .out({out_153, out_154, out_155, out_156, out_157, out_158, out_159, out_160, out_161, out_162, out_163, out_164, out_165, out_166, out_167, out_168}),
    .sel(in_1));  // open: in0, in1, in3
  Multiplexer #(.select(2), .width(16), .enable("false")) multiplexer_3 (
    .in2(M6),
    .out({out_169, out_170, out_171, out_172, out_173, out_174, out_175, out_176, out_177, out_178, out_179, out_180, out_181, out_182, out_183, out_184}),
    .sel(in_1));  // open: in0, in1, in3
  Multiplexer #(.select(2), .width(16), .enable("false")) multiplexer_4 (
    .in0({{15{in_135}}, A5[0]}), .in1({{15{in_136}}, S5[0]}), .in2(M5),
    .out({out_185, out_186, out_187, out_188, out_189, out_190, out_191, out_192, out_193, out_194, out_195, out_196, out_197, out_198, out_199, out_200}),
    .sel(in_1));  // open: in3
  Multiplexer #(.select(2), .width(16), .enable("false")) multiplexer_5 (
    .in0(A4), .in1(S4), .in2(M4),
    .out({out_201, out_202, out_203, out_204, out_205, out_206, out_207, out_208, out_209, out_210, out_211, out_212, out_213, out_214, out_215, out_216}),
    .sel(in_1));  // open: in3
  Multiplexer #(.select(2), .width(16), .enable("false")) multiplexer_6 (
    .in0(A3), .in1(S3), .in2(M3),
    .out({out_217, out_218, out_219, out_220, out_221, out_222, out_223, out_224, out_225, out_226, out_227, out_228, out_229, out_230, out_231, out_232}),
    .sel(in_1));  // open: in3
  Multiplexer #(.select(2), .width(16), .enable("false")) multiplexer_7 (
    .in0(A2), .in1(S2), .in2(M2),
    .out({out_233, out_234, out_235, out_236, out_237, out_238, out_239, out_240, out_241, out_242, out_243, out_244, out_245, out_246, out_247, out_248}),
    .sel(in_1));  // open: in3
  Multiplexer #(.select(2), .width(16), .enable("false")) multiplexer_8 (
    .in0(A1), .in1(S1), .in2(AE0),
    .out({out_249, out_250, out_251, out_252, out_253, out_254, out_255, out_256, out_257, out_258, out_259, out_260, out_261, out_262, out_263, out_264}),
    .sel(in_1));  // open: in3
  Multiplier #(.width(16)) multiplier_1 (
    .a({in_50, in_51, in_52, in_53, in_54, in_55, in_56, in_57, in_58, in_59, in_60, in_61, in_62, in_63, in_64, in_65}),
    .b({in_114, in_115, in_116, in_117, in_118, in_119, in_120, in_121, in_122, in_123, in_124, in_125, in_126, in_127, in_128, in_129}),
    .out(AE0), .cout(AE1));  // open: cin
  Multiplier #(.width(16)) multiplier_2 (
    .a({in_114, in_115, in_116, in_117, in_118, in_119, in_120, in_121, in_122, in_123, in_124, in_125, in_126, in_127, in_128, in_129}),
    .b({in_34, in_35, in_36, in_37, in_38, in_39, in_40, in_41, in_42, in_43, in_44, in_45, in_46, in_47, in_48, in_49}),
    .out(EB0), .cout(EB1));  // open: cin
  Multiplier #(.width(16)) multiplier_3 (
    .a({in_98, in_99, in_100, in_101, in_102, in_103, in_104, in_105, in_106, in_107, in_108, in_109, in_110, in_111, in_112, in_113}),
    .b({in_50, in_51, in_52, in_53, in_54, in_55, in_56, in_57, in_58, in_59, in_60, in_61, in_62, in_63, in_64, in_65}),
    .out(FA0), .cout(FA1));  // open: cin
  Multiplier #(.width(16)) multiplier_4 (
    .a({in_114, in_115, in_116, in_117, in_118, in_119, in_120, in_121, in_122, in_123, in_124, in_125, in_126, in_127, in_128, in_129}),
    .b({in_18, in_19, in_20, in_21, in_22, in_23, in_24, in_25, in_26, in_27, in_28, in_29, in_30, in_31, in_32, in_33}),
    .out(EC0), .cout(EC1));  // open: cin
  Multiplier #(.width(16)) multiplier_5 (
    .a({in_98, in_99, in_100, in_101, in_102, in_103, in_104, in_105, in_106, in_107, in_108, in_109, in_110, in_111, in_112, in_113}),
    .b({in_34, in_35, in_36, in_37, in_38, in_39, in_40, in_41, in_42, in_43, in_44, in_45, in_46, in_47, in_48, in_49}),
    .out(FB0), .cout(FB1));  // open: cin
  Multiplier #(.width(16)) multiplier_6 (
    .a({in_82, in_83, in_84, in_85, in_86, in_87, in_88, in_89, in_90, in_91, in_92, in_93, in_94, in_95, in_96, in_97}),
    .b({in_50, in_51, in_52, in_53, in_54, in_55, in_56, in_57, in_58, in_59, in_60, in_61, in_62, in_63, in_64, in_65}),
    .out(GA0), .cout(GA1));  // open: cin
  Multiplier #(.width(16)) multiplier_7 (
    .a({in_114, in_115, in_116, in_117, in_118, in_119, in_120, in_121, in_122, in_123, in_124, in_125, in_126, in_127, in_128, in_129}),
    .b({in_2, in_3, in_4, in_5, in_6, in_7, in_8, in_9, in_10, in_11, in_12, in_13, in_14, in_15, in_16, in_17}),
    .out(ED0), .cout(ED1));  // open: cin
  Multiplier #(.width(16)) multiplier_8 (
    .a({in_98, in_99, in_100, in_101, in_102, in_103, in_104, in_105, in_106, in_107, in_108, in_109, in_110, in_111, in_112, in_113}),
    .b({in_18, in_19, in_20, in_21, in_22, in_23, in_24, in_25, in_26, in_27, in_28, in_29, in_30, in_31, in_32, in_33}),
    .out(FC0), .cout(FC1));  // open: cin
  Multiplier #(.width(16)) multiplier_9 (
    .a({in_82, in_83, in_84, in_85, in_86, in_87, in_88, in_89, in_90, in_91, in_92, in_93, in_94, in_95, in_96, in_97}),
    .b({in_34, in_35, in_36, in_37, in_38, in_39, in_40, in_41, in_42, in_43, in_44, in_45, in_46, in_47, in_48, in_49}),
    .out(GB0), .cout(GB1));  // open: cin
  Multiplier #(.width(16)) multiplier_10 (
    .a({in_66, in_67, in_68, in_69, in_70, in_71, in_72, in_73, in_74, in_75, in_76, in_77, in_78, in_79, in_80, in_81}),
    .b({in_50, in_51, in_52, in_53, in_54, in_55, in_56, in_57, in_58, in_59, in_60, in_61, in_62, in_63, in_64, in_65}),
    .out(HA0), .cout(HA1));  // open: cin
  Multiplier #(.width(16)) multiplier_11 (
    .a({in_98, in_99, in_100, in_101, in_102, in_103, in_104, in_105, in_106, in_107, in_108, in_109, in_110, in_111, in_112, in_113}),
    .b({in_2, in_3, in_4, in_5, in_6, in_7, in_8, in_9, in_10, in_11, in_12, in_13, in_14, in_15, in_16, in_17}),
    .out(FD0), .cout(FD1));  // open: cin
  Multiplier #(.width(16)) multiplier_12 (
    .a({in_82, in_83, in_84, in_85, in_86, in_87, in_88, in_89, in_90, in_91, in_92, in_93, in_94, in_95, in_96, in_97}),
    .b({in_18, in_19, in_20, in_21, in_22, in_23, in_24, in_25, in_26, in_27, in_28, in_29, in_30, in_31, in_32, in_33}),
    .out(GC0), .cout(GC1));  // open: cin
  Multiplier #(.width(16)) multiplier_13 (
    .a({in_66, in_67, in_68, in_69, in_70, in_71, in_72, in_73, in_74, in_75, in_76, in_77, in_78, in_79, in_80, in_81}),
    .b({in_34, in_35, in_36, in_37, in_38, in_39, in_40, in_41, in_42, in_43, in_44, in_45, in_46, in_47, in_48, in_49}),
    .out(HB0), .cout(HB1));  // open: cin
  Multiplier #(.width(16)) multiplier_14 (
    .a({in_82, in_83, in_84, in_85, in_86, in_87, in_88, in_89, in_90, in_91, in_92, in_93, in_94, in_95, in_96, in_97}),
    .b({in_2, in_3, in_4, in_5, in_6, in_7, in_8, in_9, in_10, in_11, in_12, in_13, in_14, in_15, in_16, in_17}),
    .out(GD0), .cout(GD1));  // open: cin
  Multiplier #(.width(16)) multiplier_15 (
    .a({in_66, in_67, in_68, in_69, in_70, in_71, in_72, in_73, in_74, in_75, in_76, in_77, in_78, in_79, in_80, in_81}),
    .b({in_18, in_19, in_20, in_21, in_22, in_23, in_24, in_25, in_26, in_27, in_28, in_29, in_30, in_31, in_32, in_33}),
    .out(HC0), .cout(HC1));  // open: cin
  Multiplier #(.width(16)) multiplier_16 (
    .a({in_66, in_67, in_68, in_69, in_70, in_71, in_72, in_73, in_74, in_75, in_76, in_77, in_78, in_79, in_80, in_81}),
    .b({in_2, in_3, in_4, in_5, in_6, in_7, in_8, in_9, in_10, in_11, in_12, in_13, in_14, in_15, in_16, in_17}),
    .out(HD0), .cout(HD1));  // open: cin
  Adder #(.width(16)) adder_1 (.a(AE1), .b(EB0), .out(adder_1_out), .cout(adder_1_cout));  // open: cin
  Adder #(.width(16)) adder_2 (.a(EB1), .b(FA1), .out(adder_2_out), .cin(adder_1_cout), .cout(adder_2_cout));
  Adder #(.width(16)) adder_3 (.a(EC1), .b(FB1), .out(adder_3_out), .cin(adder_2_cout), .cout(adder_3_cout));
  Adder #(.width(16)) adder_4 (.a(ED1), .b(FC1), .out(adder_4_out), .cin(adder_3_cout), .cout(adder_4_cout));
  Adder #(.width(16)) adder_5 (.a(FD1), .b(GC1), .out(adder_5_out), .cin(adder_4_cout), .cout(adder_5_cout));
  Adder #(.width(16)) adder_6 (.a(GD1), .b(HC1), .out(adder_6_out), .cin(adder_5_cout), .cout(adder_6_cout));
  Adder #(.width(16)) adder_7 (
    .a(HD1), .b({{15{in_133}}, adder_13_cout[0]}), .out(adder_7_out), .cin(adder_6_cout));  // open: cout
  Adder #(.width(16)) adder_8 (.a(adder_1_out), .b(FA0), .out(M2), .cout(adder_8_cout));  // open: cin
  Adder #(.width(16)) adder_9 (.a(adder_2_out), .b(EC0), .out(adder_9_out), .cin(adder_8_cout), .cout(adder_9_cout));
  Adder #(.width(16)) adder_10 (.a(adder_3_out), .b(GA1), .out(adder_10_out), .cin(adder_9_cout), .cout(adder_10_cout));
  Adder #(.width(16)) adder_11 (
    .a(adder_4_out), .b(GB1), .out(adder_11_out), .cin(adder_10_cout), .cout(adder_11_cout));
  Adder #(.width(16)) adder_12 (
    .a(adder_5_out), .b(HB1), .out(adder_12_out), .cin(adder_11_cout), .cout(adder_12_cout));
  Adder #(.width(16)) adder_13 (
    .a(adder_6_out), .b(HD0), .out(adder_13_out), .cin(adder_12_cout), .cout(adder_13_cout[0]));
  Adder #(.width(16)) adder_14 (
    .a({in_50, in_51, in_52, in_53, in_54, in_55, in_56, in_57, in_58, in_59, in_60, in_61, in_62, in_63, in_64, in_65}),
    .b({in_114, in_115, in_116, in_117, in_118, in_119, in_120, in_121, in_122, in_123, in_124, in_125, in_126, in_127, in_128, in_129}),
    .out(A1), .cout(adder_14_cout));  // open: cin
  Adder #(.width(16)) adder_15 (
    .a({in_34, in_35, in_36, in_37, in_38, in_39, in_40, in_41, in_42, in_43, in_44, in_45, in_46, in_47, in_48, in_49}),
    .b({in_98, in_99, in_100, in_101, in_102, in_103, in_104, in_105, in_106, in_107, in_108, in_109, in_110, in_111, in_112, in_113}),
    .out(A2), .cin(adder_14_cout), .cout(adder_15_cout));
  Adder #(.width(16)) adder_16 (
    .a({in_18, in_19, in_20, in_21, in_22, in_23, in_24, in_25, in_26, in_27, in_28, in_29, in_30, in_31, in_32, in_33}),
    .b({in_82, in_83, in_84, in_85, in_86, in_87, in_88, in_89, in_90, in_91, in_92, in_93, in_94, in_95, in_96, in_97}),
    .out(A3), .cin(adder_15_cout), .cout(adder_16_cout));
  Adder #(.width(16)) adder_17 (
    .a({in_2, in_3, in_4, in_5, in_6, in_7, in_8, in_9, in_10, in_11, in_12, in_13, in_14, in_15, in_16, in_17}),
    .b({in_66, in_67, in_68, in_69, in_70, in_71, in_72, in_73, in_74, in_75, in_76, in_77, in_78, in_79, in_80, in_81}),
    .out(A4), .cin(adder_16_cout), .cout(A5[0]));
  Subtractor #(.width(16)) subtractor_1 (
    .a({in_50, in_51, in_52, in_53, in_54, in_55, in_56, in_57, in_58, in_59, in_60, in_61, in_62, in_63, in_64, in_65}),
    .b({in_114, in_115, in_116, in_117, in_118, in_119, in_120, in_121, in_122, in_123, in_124, in_125, in_126, in_127, in_128, in_129}),
    .out(S1), .bout(subtractor_1_bout));  // open: bin
  Subtractor #(.width(16)) subtractor_2 (
    .a({in_34, in_35, in_36, in_37, in_38, in_39, in_40, in_41, in_42, in_43, in_44, in_45, in_46, in_47, in_48, in_49}),
    .b({in_98, in_99, in_100, in_101, in_102, in_103, in_104, in_105, in_106, in_107, in_108, in_109, in_110, in_111, in_112, in_113}),
    .out(S2), .bin(subtractor_1_bout), .bout(subtractor_2_bout));
  Subtractor #(.width(16)) subtractor_3 (
    .a({in_18, in_19, in_20, in_21, in_22, in_23, in_24, in_25, in_26, in_27, in_28, in_29, in_30, in_31, in_32, in_33}),
    .b({in_82, in_83, in_84, in_85, in_86, in_87, in_88, in_89, in_90, in_91, in_92, in_93, in_94, in_95, in_96, in_97}),
    .out(S3), .bin(subtractor_2_bout), .bout(subtractor_3_bout));
  Subtractor #(.width(16)) subtractor_4 (
    .a({in_2, in_3, in_4, in_5, in_6, in_7, in_8, in_9, in_10, in_11, in_12, in_13, in_14, in_15, in_16, in_17}),
    .b({in_66, in_67, in_68, in_69, in_70, in_71, in_72, in_73, in_74, in_75, in_76, in_77, in_78, in_79, in_80, in_81}),
    .out(S4), .bin(subtractor_3_bout), .bout(S5[0]));
  Adder #(.width(16)) adder_18 (.a(adder_9_out), .b(FB0), .out(adder_18_out), .cout(adder_18_cout));  // open: cin
  Adder #(.width(16)) adder_19 (
    .a(adder_10_out), .b(ED0), .out(adder_19_out), .cin(adder_18_cout), .cout(adder_19_cout));
  Adder #(.width(16)) adder_20 (
    .a(adder_11_out), .b(HA1), .out(adder_20_out), .cin(adder_19_cout), .cout(adder_20_cout));
  Adder #(.width(16)) adder_21 (
    .a(adder_12_out), .b(GD0), .out(adder_21_out), .cin(adder_20_cout), .cout(adder_21_cout));
  Adder #(.width(16)) adder_22 (
    .a({{15{in_131}}, adder_27_cout[0]}), .b(adder_13_out), .out(adder_22_out), .cin(adder_21_cout),
    .cout(adder_22_cout));
  Adder #(.width(16)) adder_23 (
    .a(adder_7_out), .b({{15{in_134}}, adder_28_cout[0]}), .out(M8), .cin(adder_22_cout));  // open: cout
  Adder #(.width(16)) adder_24 (.a(adder_18_out), .b(GA0), .out(M3), .cout(adder_24_cout));  // open: cin
  Adder #(.width(16)) adder_25 (
    .a(adder_19_out), .b(FC0), .out(adder_25_out), .cin(adder_24_cout), .cout(adder_25_cout));
  Adder #(.width(16)) adder_26 (
    .a(adder_20_out), .b(FD0), .out(adder_26_out), .cin(adder_25_cout), .cout(adder_26_cout));
  Adder #(.width(16)) adder_27 (
    .a(adder_21_out), .b(HC0), .out(adder_27_out), .cin(adder_26_cout), .cout(adder_27_cout[0]));
  Adder #(.width(16)) adder_28 (
    .a({{15{in_132}}, adder_31_cout[0]}), .b(adder_22_out), .out(M7), .cout(adder_28_cout[0]));  // open: cin
  Adder #(.width(16)) adder_29 (.a(adder_25_out), .b(GB0), .out(adder_29_out), .cout(adder_29_cout));  // open: cin
  Adder #(.width(16)) adder_30 (
    .a(adder_26_out), .b(GC0), .out(adder_30_out), .cin(adder_29_cout), .cout(adder_30_cout));
  Adder #(.width(16)) adder_31 (
    .a({{15{in_130}}, adder_33_cout[0]}), .b(adder_27_out), .out(M6), .cin(adder_30_cout),
    .cout(adder_31_cout[0]));
  Adder #(.width(16)) adder_32 (.a(adder_29_out), .b(HA0), .out(M4), .cout(adder_32_cout));  // open: cin
  Adder #(.width(16)) adder_33 (.a(adder_30_out), .b(HB0), .out(M5), .cin(adder_32_cout), .cout(adder_33_cout[0]));

  assign out_266 = {out_137, out_138, out_139, out_140, out_141, out_142, out_143, out_144, out_145, out_146, out_147, out_148, out_149, out_150, out_151, out_152};
  assign out_267 = {out_153, out_154, out_155, out_156, out_157, out_158, out_159, out_160, out_161, out_162, out_163, out_164, out_165, out_166, out_167, out_168};
  assign out_268 = {out_169, out_170, out_171, out_172, out_173, out_174, out_175, out_176, out_177, out_178, out_179, out_180, out_181, out_182, out_183, out_184};
  assign out_269 = {out_185, out_186, out_187, out_188, out_189, out_190, out_191, out_192, out_193, out_194, out_195, out_196, out_197, out_198, out_199, out_200};
  assign out_270 = {out_201, out_202, out_203, out_204, out_205, out_206, out_207, out_208, out_209, out_210, out_211, out_212, out_213, out_214, out_215, out_216};
  assign out_271 = {out_217, out_218, out_219, out_220, out_221, out_222, out_223, out_224, out_225, out_226, out_227, out_228, out_229, out_230, out_231, out_232};
  assign out_272 = {out_233, out_234, out_235, out_236, out_237, out_238, out_239, out_240, out_241, out_242, out_243, out_244, out_245, out_246, out_247, out_248};
  assign out_273 = {out_249, out_250, out_251, out_252, out_253, out_254, out_255, out_256, out_257, out_258, out_259, out_260, out_261, out_262, out_263, out_264};

  // Other names for the same wires on the sheet: A[15:0] = {in_50, in_51, in_52, in_53, in_54, in_55, in_56, in_57, in_58, in_59, in_60, in_61, in_62, in_63, in_64, in_65};
  //   A5[15:1] = {15{in_135}};
  //   B[15:0] = {in_34, in_35, in_36, in_37, in_38, in_39, in_40, in_41, in_42, in_43, in_44, in_45, in_46, in_47, in_48, in_49};
  //   C[15:0] = {in_18, in_19, in_20, in_21, in_22, in_23, in_24, in_25, in_26, in_27, in_28, in_29, in_30, in_31, in_32, in_33};
  //   Controller[1:0] = in_1;
  //   D[15:0] = {in_2, in_3, in_4, in_5, in_6, in_7, in_8, in_9, in_10, in_11, in_12, in_13, in_14, in_15, in_16, in_17};
  //   E[15:0] = {in_114, in_115, in_116, in_117, in_118, in_119, in_120, in_121, in_122, in_123, in_124, in_125, in_126, in_127, in_128, in_129};
  //   F[15:0] = {in_98, in_99, in_100, in_101, in_102, in_103, in_104, in_105, in_106, in_107, in_108, in_109, in_110, in_111, in_112, in_113};
  //   G[15:0] = {in_82, in_83, in_84, in_85, in_86, in_87, in_88, in_89, in_90, in_91, in_92, in_93, in_94, in_95, in_96, in_97};
  //   H[15:0] = {in_66, in_67, in_68, in_69, in_70, in_71, in_72, in_73, in_74, in_75, in_76, in_77, in_78, in_79, in_80, in_81};
  //   M1[15:0] = AE0;
  //   P1[15:0] = {out_249, out_250, out_251, out_252, out_253, out_254, out_255, out_256, out_257, out_258, out_259, out_260, out_261, out_262, out_263, out_264};
  //   P2[15:0] = {out_233, out_234, out_235, out_236, out_237, out_238, out_239, out_240, out_241, out_242, out_243, out_244, out_245, out_246, out_247, out_248};
  //   P3[15:0] = {out_217, out_218, out_219, out_220, out_221, out_222, out_223, out_224, out_225, out_226, out_227, out_228, out_229, out_230, out_231, out_232};
  //   P4[15:0] = {out_201, out_202, out_203, out_204, out_205, out_206, out_207, out_208, out_209, out_210, out_211, out_212, out_213, out_214, out_215, out_216};
  //   P5[15:0] = {out_185, out_186, out_187, out_188, out_189, out_190, out_191, out_192, out_193, out_194, out_195, out_196, out_197, out_198, out_199, out_200};
  //   P6[15:0] = {out_169, out_170, out_171, out_172, out_173, out_174, out_175, out_176, out_177, out_178, out_179, out_180, out_181, out_182, out_183, out_184};
  //   P7[15:0] = {out_153, out_154, out_155, out_156, out_157, out_158, out_159, out_160, out_161, out_162, out_163, out_164, out_165, out_166, out_167, out_168};
  //   P8[15:0] = {out_137, out_138, out_139, out_140, out_141, out_142, out_143, out_144, out_145, out_146, out_147, out_148, out_149, out_150, out_151, out_152};
  //   S5[15:1] = {15{in_136}}

  // Notes on the sheet:
  //   NOTE
  //   Subtraction
  //   Multiplication
  //   : Mean Don't Take it in OUTPUT
  //   Controller
  //   Addition
  //   00
  //   01
  //   10
  //   INPUT
  //   OUTPUT
  //   Multiplication Circuit
  //   Addition Circuit
  //   Subtraction Circuit
endmodule
